# Fritzing sketch CircuitDiagram (saved by Fritzing 0.9.3b)
breadboards: 1

parts:
  Componente2 = RFID-RC522-v2
  U1 = 2-Channel 5v Relay Shield [package=relay-2ch5v10a]
  S1 = Pushbutton [package="[THT]"]
  Raspberry_Pi1 = Raspberry Pi Zero
  JACK1 = 2.1mm Barrel Jack with Terminal Block

nets:
  N1: Componente2.SDA, Raspberry_Pi1.GIPO8
  N2: Componente2.SCK, Raspberry_Pi1.GIPO11
  N3: Componente2.MOSI, Raspberry_Pi1.GIPO10
  N4: Componente2.MISO, Raspberry_Pi1.GIPO9
  GND: Componente2.GND, U1.GND, S1.Pin_1, S1.Pin_2, Raspberry_Pi1.GND
  N5: Componente2.RST, Raspberry_Pi1.GIPO25
  3.3V: Componente2.3.3V, Raspberry_Pi1.3v3
  VCC: U1.VCC, Raspberry_Pi1.5V
  N6: U1.IN1, Raspberry_Pi1.GIPO17
  N7: U1.K1-Off, JACK1.POS
  N8: S1.Pin_3, S1.Pin_4, Raspberry_Pi1.GIPO27

notes:
  Connects to 12V + Terminal of magnetic door lock
  Connects to 12V GND Terminal of magnetic door lock
  Connects to 12V power supply

custom parts:
  RFID-RC522-v2: A simple China made RFID-RC522 Reader; do check the pin labels, as this is a MFRC522 based clone.
  2-Channel 5v Relay Shield: 2 Channel 5v Relay Shield w. 2x SPD-06VDC-SD-C
  Raspberry Pi Zero: The Raspberry Pi Zero is the latest single board computer to be released by the Raspberry Pi Foundation. It is the entry level model Raspberry Pi perfect for hobbyists, makers and industrial engineers looking to create solutions where small size and low power consumption are important. This is especially relevant for applications in the wearables space as well as up and coming applications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
